// Logisim project P0.L0.Q1.circ as structural Verilog: 3 circuits, main circuit main
module main (
  output [10:0] out_1
);
endmodule

module mod2 (
  input  [3:0] A,
  input  [3:0] B,
  output [2:0] C,
  output D
);

  wire and_1_out, and_2_out, and_3_out, and_4_out, and_5_out, and_6_out, not_1_out, xor_1_out, xor_2_out,
       xor_3_out;

  or or_1 (D, 1'b0, A[3]);
  xor xor_1 (xor_1_out, A[0], B[0]);
  xor xor_2 (xor_2_out, A[1], B[1]);
  xor xor_3 (xor_3_out, A[2], B[2]);
  not not_1 (not_1_out, D);
  and and_1 (and_1_out, not_1_out, A[0]);
  and and_2 (and_2_out, not_1_out, A[1]);
  and and_3 (and_3_out, not_1_out, A[2]);
  and and_4 (and_4_out, xor_1_out, D);
  and and_5 (and_5_out, D, xor_2_out);
  and and_6 (and_6_out, xor_3_out, D);
  or or_2 (C[0], and_1_out, and_4_out);
  or or_3 (C[1], and_2_out, and_5_out);
  or or_4 (C[2], and_3_out, and_6_out);
endmodule

module CRC (
  input  [7:0] A,
  input  [3:0] B,
  output [10:0] out_3
);

  wire [2:0] mod2_1_c, mod2_2_c, mod2_4_c, mod2_5_c, mod2_6_c, mod2_7_c;
  wire [3:1] mod2_3_c;

  // Probe on A[7:4]
  mod2 mod2_1 (.A(A[7:4]), .B(B), .C(mod2_1_c));  // open: D
  // Probe on mod2_1_c
  // Probe on {mod2_1_c, A[3]}
  // Probe on mod2_2_c
  mod2 mod2_2 (.A({mod2_1_c, A[3]}), .B(B), .C(mod2_2_c));  // open: D
  // Probe on {mod2_2_c, A[2]}
  // Probe on mod2_3_c
  mod2 mod2_3 (.A({mod2_2_c, A[2]}), .B(B), .C(mod2_3_c));  // open: D
  // Probe on {mod2_3_c, A[1]}
  // Probe on mod2_4_c
  mod2 mod2_4 (.A({mod2_3_c, A[1]}), .B(B), .C(mod2_4_c));  // open: D
  // Probe on {mod2_4_c, A[0]}
  mod2 mod2_5 (.A({mod2_4_c, A[0]}), .B(B), .C(mod2_5_c));  // open: D
  // Probe on {mod2_5_c, 1'b0}
  // Probe on mod2_5_c
  // Probe on mod2_6_c
  mod2 mod2_6 (.A({mod2_5_c, 1'b0}), .B(B), .C(mod2_6_c));  // open: D
  // Probe on {mod2_6_c, 1'b0}
  // Probe on mod2_7_c
  mod2 mod2_7 (.A({mod2_6_c, 1'b0}), .B(B), .C(mod2_7_c));  // open: D
  // Probe on out_3[2:0]
  mod2 mod2_8 (.A({mod2_7_c, 1'b0}), .B(B), .C(out_3[2:0]));  // open: D

  assign out_3[10:3] = A;
endmodule
