// Logisim project P0.L0.Q3.circ as structural Verilog
module grf (
  input  reset,
  input  [4:0] A1,
  input  in_3,
  input  WE,
  input  [4:0] A2,
  input  [4:0] A3,
  input  [31:0] WD,
  output [31:0] RD1,
  output [31:0] RD2
);

  wire comparator_1_eq, comparator_2_eq, comparator_2_lt, comparator_3_eq, comparator_4_eq, comparator_5_eq,
       comparator_6_eq, comparator_7_eq, comparator_8_eq, comparator_9_eq, comparator_10_eq,
       comparator_11_eq, comparator_12_eq, comparator_13_eq, comparator_14_eq, comparator_15_eq,
       comparator_16_eq, comparator_17_eq, comparator_18_eq, comparator_19_eq, comparator_20_eq,
       comparator_21_eq, comparator_22_eq, comparator_23_eq, comparator_24_eq, comparator_25_eq,
       comparator_26_eq, comparator_27_eq, comparator_28_eq, comparator_29_eq, comparator_30_eq,
       comparator_31_eq, re, undriven;
  wire [4:0] a1_t, a2_t, a3_t;
  wire [31:0] _0, _1, _2, _3, _4, _5, _6, _7, _8, _9, _10, _11, _12, _13, _14, _15, _16, _17, _18, _19, _20,
       _21, _22, _23, _24, _25, _26, _27, _28, _29, _30, _31, in1, in2, in3, in4, in5, in6, in7, in8, in9,
       in10, in11, in12, in13, in14, in15, in16, in17, in18, in19, in20, in21, in22, in23, in24, in25, in26,
       in27, in28, in29, in30, in31, multiplexer_1_out, multiplexer_2_out, multiplexer_3_out,
       multiplexer_4_out, multiplexer_5_out, multiplexer_6_out, multiplexer_7_out, multiplexer_8_out,
       multiplexer_9_out, multiplexer_10_out, multiplexer_11_out, multiplexer_12_out, multiplexer_13_out,
       multiplexer_14_out, multiplexer_29_out, multiplexer_30_out, multiplexer_31_out, multiplexer_32_out,
       multiplexer_33_out, multiplexer_34_out, multiplexer_35_out, multiplexer_36_out, multiplexer_37_out,
       multiplexer_38_out, multiplexer_51_out, multiplexer_52_out, multiplexer_53_out, multiplexer_54_out,
       multiplexer_55_out, multiplexer_56_out, multiplexer_57_out, wd_t;

  Register #(.width(5)) register_1 (.D(A3), .Q(a3_t), .clk(in_3));  // open: en, clr
  Register #(.width(5)) register_2 (.D(A1), .Q(a1_t), .clk(in_3));  // open: en, clr
  Register #(.width(5)) register_3 (.D(A2), .Q(a2_t), .clk(in_3));  // open: en, clr
  Register #(.width(32)) register_4 (.D(WD), .Q(wd_t), .clk(in_3));  // open: en, clr
  Register #(.width(32)) register_5 (.D({32{1'b0}}), .en(WE), .Q(_0), .clk(in_3), .clr(re));
  Register #(.width(32)) register_6 (.D(in4), .en(WE), .Q(_4), .clk(in_3), .clr(re));
  Register #(.width(32)) register_7 (.D(in8), .en(WE), .Q(_8), .clk(in_3), .clr(re));
  Register #(.width(32)) register_8 (.D(in12), .en(WE), .Q(_12), .clk(in_3), .clr(re));
  Register #(.width(32)) register_9 (.D(in16), .en(WE), .Q(_16), .clk(in_3), .clr(re));
  Register #(.width(32)) register_10 (.D(in20), .en(WE), .Q(_20), .clk(in_3), .clr(re));
  Register #(.width(32)) register_11 (.D(in24), .en(WE), .Q(_24), .clk(in_3), .clr(re));
  Register #(.width(32)) register_12 (.D(in28), .en(WE), .Q(_28), .clk(in_3), .clr(re));
  Comparator #(.width(5)) comparator_1 (.a(a3_t), .b(5'b00001), .eq(comparator_1_eq));  // open: gt, lt
  Comparator #(.width(5)) comparator_2 (
    .a(a3_t), .b(5'b00010), .eq(comparator_2_eq), .lt(comparator_2_lt));  // open: gt
  Comparator #(.width(5)) comparator_3 (.a(a3_t), .b(5'b00011), .eq(comparator_3_eq));  // open: gt, lt
  Comparator #(.width(5)) comparator_4 (.a(a3_t), .b(5'b00100), .eq(comparator_4_eq));  // open: gt, lt
  Comparator #(.width(5)) comparator_5 (.a(a3_t), .b(5'b00101), .eq(comparator_5_eq));  // open: gt, lt
  Comparator #(.width(5)) comparator_6 (.a(a3_t), .b(5'b00110), .eq(comparator_6_eq));  // open: gt, lt
  Comparator #(.width(5)) comparator_7 (.a(a3_t), .b(5'b00111), .eq(comparator_7_eq));  // open: gt, lt
  Comparator #(.width(5)) comparator_8 (.a(a3_t), .b(5'b01000), .eq(comparator_8_eq));  // open: gt, lt
  Comparator #(.width(5)) comparator_9 (.a(a3_t), .b(5'b01001), .eq(comparator_9_eq));  // open: gt, lt
  Comparator #(.width(5)) comparator_10 (.a(a3_t), .b(5'b01010), .eq(comparator_10_eq));  // open: gt, lt
  Comparator #(.width(5)) comparator_11 (.a(a3_t), .b(5'b01011), .eq(comparator_11_eq));  // open: gt, lt
  Comparator #(.width(5)) comparator_12 (.a(a3_t), .b(5'b01100), .eq(comparator_12_eq));  // open: gt, lt
  Comparator #(.width(5)) comparator_13 (.a(a3_t), .b(5'b01101), .eq(comparator_13_eq));  // open: gt, lt
  Comparator #(.width(5)) comparator_14 (.a(a3_t), .b(5'b01110), .eq(comparator_14_eq));  // open: gt, lt
  Register #(.width(1)) register_13 (.D(reset), .Q(re), .clk(in_3));  // open: en, clr
  Register #(.width(32)) register_14 (.D(in1), .en(WE), .Q(_1), .clk(in_3), .clr(re));
  Register #(.width(32)) register_15 (.D(in5), .en(WE), .Q(_5), .clk(in_3), .clr(re));
  Register #(.width(32)) register_16 (.D(in9), .en(WE), .Q(_9), .clk(in_3), .clr(re));
  Register #(.width(32)) register_17 (.D(in13), .en(WE), .Q(_13), .clk(in_3), .clr(re));
  Register #(.width(32)) register_18 (.D(in17), .en(WE), .Q(_17), .clk(in_3), .clr(re));
  Register #(.width(32)) register_19 (.D(in21), .en(WE), .Q(_21), .clk(in_3), .clr(re));
  Register #(.width(32)) register_20 (.D(in25), .en(WE), .Q(_25), .clk(in_3), .clr(re));
  Register #(.width(32)) register_21 (.D(in29), .en(WE), .Q(_29), .clk(in_3), .clr(re));
  Multiplexer #(.width(32)) multiplexer_1 (
    .in0(in1), .in1(wd_t), .out(multiplexer_1_out), .sel(comparator_1_eq));  // open: en
  Multiplexer #(.width(32)) multiplexer_2 (
    .in0(in2), .in1(wd_t), .out(multiplexer_2_out), .sel(comparator_2_eq));  // open: en
  Multiplexer #(.width(32)) multiplexer_3 (
    .in0(in3), .in1(wd_t), .out(multiplexer_3_out), .sel(comparator_3_eq));  // open: en
  Multiplexer #(.width(32)) multiplexer_4 (
    .in0(in4), .in1(wd_t), .out(multiplexer_4_out), .sel(comparator_4_eq));  // open: en
  Multiplexer #(.width(32)) multiplexer_5 (
    .in0(in5), .in1(wd_t), .out(multiplexer_5_out), .sel(comparator_5_eq));  // open: en
  Multiplexer #(.width(32)) multiplexer_6 (
    .in0(in6), .in1(wd_t), .out(multiplexer_6_out), .sel(comparator_6_eq));  // open: en
  Multiplexer #(.width(32)) multiplexer_7 (
    .in0(in7), .in1(wd_t), .out(multiplexer_7_out), .sel(comparator_7_eq));  // open: en
  Multiplexer #(.width(32)) multiplexer_8 (
    .in0(in8), .in1(wd_t), .out(multiplexer_8_out), .sel(comparator_8_eq));  // open: en
  Multiplexer #(.width(32)) multiplexer_9 (
    .in0(in9), .in1(wd_t), .out(multiplexer_9_out), .sel(comparator_9_eq));  // open: en
  Multiplexer #(.width(32)) multiplexer_10 (
    .in0(in10), .in1(wd_t), .out(multiplexer_10_out), .sel(comparator_10_eq));  // open: en
  Multiplexer #(.width(32)) multiplexer_11 (
    .in0(in11), .in1(wd_t), .out(multiplexer_11_out), .sel(comparator_11_eq));  // open: en
  Multiplexer #(.width(32)) multiplexer_12 (
    .in0(in12), .in1(wd_t), .out(multiplexer_12_out), .sel(comparator_12_eq));  // open: en
  Multiplexer #(.width(32)) multiplexer_13 (
    .in0(in13), .in1(wd_t), .out(multiplexer_13_out), .sel(comparator_13_eq));  // open: en
  Multiplexer #(.width(32)) multiplexer_14 (
    .in0(in14), .in1(wd_t), .out(multiplexer_14_out), .sel(comparator_14_eq));  // open: en
  Multiplexer #(.width(32)) multiplexer_15 (
    .in0(multiplexer_1_out), .in1({32{1'b0}}), .out(in1), .sel(re));  // open: en
  Multiplexer #(.width(32)) multiplexer_16 (
    .in0(multiplexer_2_out), .in1({32{1'b0}}), .out(in2), .sel(re));  // open: en
  Multiplexer #(.width(32)) multiplexer_17 (
    .in0(multiplexer_3_out), .in1({32{1'b0}}), .out(in3), .sel(re));  // open: en
  Multiplexer #(.width(32)) multiplexer_18 (
    .in0(multiplexer_4_out), .in1({32{1'b0}}), .out(in4), .sel(re));  // open: en
  Multiplexer #(.width(32)) multiplexer_19 (
    .in0(multiplexer_5_out), .in1({32{1'b0}}), .out(in5), .sel(re));  // open: en
  Multiplexer #(.width(32)) multiplexer_20 (
    .in0(multiplexer_6_out), .in1({32{1'b0}}), .out(in6), .sel(re));  // open: en
  Multiplexer #(.width(32)) multiplexer_21 (
    .in0(multiplexer_7_out), .in1({32{1'b0}}), .out(in7), .sel(re));  // open: en
  Multiplexer #(.width(32)) multiplexer_22 (
    .in0(multiplexer_8_out), .in1({32{1'b0}}), .out(in8), .sel(re));  // open: en
  Multiplexer #(.width(32)) multiplexer_23 (
    .in0(multiplexer_9_out), .in1({32{1'b0}}), .out(in9), .sel(re));  // open: en
  Multiplexer #(.width(32)) multiplexer_24 (
    .in0(multiplexer_10_out), .in1({32{1'b0}}), .out(in10), .sel(re));  // open: en
  Multiplexer #(.width(32)) multiplexer_25 (
    .in0(multiplexer_11_out), .in1({32{1'b0}}), .out(in11), .sel(re));  // open: en
  Multiplexer #(.width(32)) multiplexer_26 (
    .in0(multiplexer_12_out), .in1({32{1'b0}}), .out(in12), .sel(re));  // open: en
  Multiplexer #(.width(32)) multiplexer_27 (
    .in0(multiplexer_13_out), .in1({32{1'b0}}), .out(in13), .sel(re));  // open: en
  Multiplexer #(.width(32)) multiplexer_28 (
    .in0(multiplexer_14_out), .in1({32{1'b0}}), .out(in14), .sel(re));  // open: en
  Register #(.width(32)) register_22 (.D(in2), .en(WE), .Q(_2), .clk(in_3), .clr(re));
  Register #(.width(32)) register_23 (.D(in6), .en(WE), .Q(_6), .clk(in_3), .clr(re));
  Register #(.width(32)) register_24 (.D(in10), .en(WE), .Q(_10), .clk(in_3), .clr(re));
  Register #(.width(32)) register_25 (.D(in14), .en(WE), .Q(_14), .clk(in_3), .clr(re));
  Register #(.width(32)) register_26 (.D(in18), .en(WE), .Q(_18), .clk(in_3), .clr(re));
  Register #(.width(32)) register_27 (.D(in22), .en(WE), .Q(_22), .clk(in_3), .clr(re));
  Register #(.width(32)) register_28 (.D(in26), .en(WE), .Q(_26), .clk(in_3), .clr(re));
  Register #(.width(32)) register_29 (.D(in30), .en(WE), .Q(_30), .clk(in_3), .clr(re));
  Register #(.width(32)) register_30 (.D(in3), .en(WE), .Q(_3), .clk(in_3), .clr(re));
  Register #(.width(32)) register_31 (.D(in7), .en(WE), .Q(_7), .clk(in_3), .clr(re));
  Register #(.width(32)) register_32 (.D(in11), .en(WE), .Q(_11), .clk(in_3), .clr(re));
  Register #(.width(32)) register_33 (.D(in15), .en(WE), .Q(_15), .clk(in_3), .clr(re));
  Register #(.width(32)) register_34 (.D(in19), .en(WE), .Q(_19), .clk(in_3), .clr(re));
  Register #(.width(32)) register_35 (.D(in23), .en(WE), .Q(_23), .clk(in_3), .clr(re));
  Register #(.width(32)) register_36 (.D(in27), .en(WE), .Q(_27), .clk(in_3), .clr(re));
  Register #(.width(32)) register_37 (.D(in31), .en(WE), .Q(_31), .clk(in_3), .clr(re));
  Comparator #(.width(5)) comparator_15 (.a(a3_t), .b(5'b01111), .eq(comparator_15_eq));  // open: gt, lt
  Comparator #(.width(5)) comparator_16 (.a(a3_t), .b(5'b10000), .eq(comparator_16_eq));  // open: gt, lt
  Comparator #(.width(5)) comparator_17 (.a(a3_t), .b(5'b10001), .eq(comparator_17_eq));  // open: gt, lt
  Comparator #(.width(5)) comparator_18 (.a(a3_t), .b(5'b10010), .eq(comparator_18_eq));  // open: gt, lt
  Comparator #(.width(5)) comparator_19 (.a(a3_t), .b(5'b10011), .eq(comparator_19_eq));  // open: gt, lt
  Comparator #(.width(5)) comparator_20 (.a(a3_t), .b(5'b10100), .eq(comparator_20_eq));  // open: gt, lt
  Comparator #(.width(5)) comparator_21 (.a(a3_t), .b(5'b10101), .eq(comparator_21_eq));  // open: gt, lt
  Comparator #(.width(5)) comparator_22 (.a(a3_t), .b(5'b10110), .eq(comparator_22_eq));  // open: gt, lt
  Comparator #(.width(5)) comparator_23 (.a(a3_t), .b(5'b10111), .eq(comparator_23_eq));  // open: gt, lt
  Comparator #(.width(5)) comparator_24 (.a(a3_t), .b(5'b11000), .eq(comparator_24_eq));  // open: gt, lt
  Multiplexer #(.width(32)) multiplexer_29 (
    .in0(in15), .in1(wd_t), .out(multiplexer_29_out), .sel(comparator_15_eq));  // open: en
  Multiplexer #(.width(32)) multiplexer_30 (
    .in0(in16), .in1(wd_t), .out(multiplexer_30_out), .sel(comparator_16_eq));  // open: en
  Multiplexer #(.width(32)) multiplexer_31 (
    .in0(in17), .in1(wd_t), .out(multiplexer_31_out), .sel(comparator_17_eq));  // open: en
  Multiplexer #(.width(32)) multiplexer_32 (
    .in0(in18), .in1(wd_t), .out(multiplexer_32_out), .sel(comparator_18_eq));  // open: en
  Multiplexer #(.width(32)) multiplexer_33 (
    .in0(in19), .in1(wd_t), .out(multiplexer_33_out), .sel(comparator_19_eq));  // open: en
  Multiplexer #(.width(32)) multiplexer_34 (
    .in0(in20), .in1(wd_t), .out(multiplexer_34_out), .sel(comparator_20_eq));  // open: en
  Multiplexer #(.width(32)) multiplexer_35 (
    .in0(in21), .in1(wd_t), .out(multiplexer_35_out), .sel(comparator_21_eq));  // open: en
  Multiplexer #(.width(32)) multiplexer_36 (
    .in0(in22), .in1(wd_t), .out(multiplexer_36_out), .sel(comparator_22_eq));  // open: en
  Multiplexer #(.width(32)) multiplexer_37 (
    .in0(in23), .in1(wd_t), .out(multiplexer_37_out), .sel(comparator_23_eq));  // open: en
  Multiplexer #(.width(32)) multiplexer_38 (
    .in0(in24), .in1(wd_t), .out(multiplexer_38_out), .sel(comparator_24_eq));  // open: en
  Multiplexer #(.width(32)) multiplexer_39 (
    .in0(multiplexer_29_out), .in1({32{1'b0}}), .out(in15), .sel(re), .en(undriven));
  Multiplexer #(.width(32)) multiplexer_40 (
    .in0(multiplexer_30_out), .in1({32{1'b0}}), .out(in16), .sel(re));  // open: en
  Multiplexer #(.width(32)) multiplexer_41 (
    .in0(multiplexer_31_out), .in1({32{1'b0}}), .out(in17), .sel(re));  // open: en
  Multiplexer #(.width(32)) multiplexer_42 (
    .in0(multiplexer_32_out), .in1({32{1'b0}}), .out(in18), .sel(re));  // open: en
  Multiplexer #(.width(32)) multiplexer_43 (
    .in0(multiplexer_33_out), .in1({32{1'b0}}), .out(in19), .sel(re));  // open: en
  Multiplexer #(.width(32)) multiplexer_44 (
    .in0(multiplexer_34_out), .in1({32{1'b0}}), .out(in20), .sel(re));  // open: en
  Multiplexer #(.width(32)) multiplexer_45 (
    .in0(multiplexer_35_out), .in1({32{1'b0}}), .out(in21), .sel(re));  // open: en
  Multiplexer #(.width(32)) multiplexer_46 (
    .in0(multiplexer_36_out), .in1({32{1'b0}}), .out(in22), .sel(re));  // open: en
  Multiplexer #(.width(32)) multiplexer_47 (
    .in0(multiplexer_37_out), .in1({32{1'b0}}), .out(in23), .sel(re));  // open: en
  Multiplexer #(.width(32)) multiplexer_48 (
    .in0(multiplexer_38_out), .in1({32{1'b0}}), .out(in24), .sel(re));  // open: en
  Multiplexer #(.select(5), .width(32)) multiplexer_49 (
    .in0(_0), .in1(_1), .in2(_2), .in3(_3), .in4(_4), .in5(_5), .in6(_6), .in7(_7), .in8(_8), .in9(_9),
    .in10(_10), .in11(_11), .in12(_12), .in13(_13), .in14(_14), .in15(_15), .in16(_16), .in17(_17),
    .in18(_18), .in19(_19), .in20(_20), .in21(_21), .in22(_22), .in23(_23), .in24(_24), .in25(_25),
    .in26(_26), .in27(_27), .in28(_28), .in29(_29), .in30(_30), .in31(_31), .out(RD1), .sel(a1_t), .en(1'b1));
  Comparator #(.width(5)) comparator_25 (.a(a3_t), .b(5'b11001), .eq(comparator_25_eq));  // open: gt, lt
  Comparator #(.width(5)) comparator_26 (.a(a3_t), .b(5'b11010), .eq(comparator_26_eq));  // open: gt, lt
  Comparator #(.width(5)) comparator_27 (.a(a3_t), .b(5'b11011), .eq(comparator_27_eq));  // open: gt, lt
  Comparator #(.width(5)) comparator_28 (.a(a3_t), .b(5'b11100), .eq(comparator_28_eq));  // open: gt, lt
  Comparator #(.width(5)) comparator_29 (.a(a3_t), .b(5'b11101), .eq(comparator_29_eq));  // open: gt, lt
  Comparator #(.width(5)) comparator_30 (.a(a3_t), .b(5'b11110), .eq(comparator_30_eq));  // open: gt, lt
  Comparator #(.width(5)) comparator_31 (.a(a3_t), .b({5{1'b1}}), .eq(comparator_31_eq));  // open: gt, lt
  Multiplexer #(.select(5), .width(32)) multiplexer_50 (
    .in0(_0), .in1(_1), .in2(_2), .in3(_3), .in4(_4), .in5(_5), .in6(_6), .in7(_7), .in8(_8), .in9(_9),
    .in10(_10), .in11(_11), .in12(_12), .in13(_13), .in14(_14), .in15(_15), .in16(_16), .in17(_17),
    .in18(_18), .in19(_19), .in20(_20), .in21(_21), .in22(_22), .in23(_23), .in24(_24), .in25(_25),
    .in26(_26), .in27(_27), .in28(_28), .in29(_29), .in30(_30), .in31(_31), .out(RD2), .sel(a2_t), .en(1'b1));
  Multiplexer #(.width(32)) multiplexer_51 (
    .in0(in25), .in1(wd_t), .out(multiplexer_51_out), .sel(comparator_25_eq));  // open: en
  Multiplexer #(.width(32)) multiplexer_52 (
    .in0(in26), .in1(wd_t), .out(multiplexer_52_out), .sel(comparator_26_eq));  // open: en
  Multiplexer #(.width(32)) multiplexer_53 (
    .in0(in27), .in1(wd_t), .out(multiplexer_53_out), .sel(comparator_27_eq));  // open: en
  Multiplexer #(.width(32)) multiplexer_54 (
    .in0(in28), .in1(wd_t), .out(multiplexer_54_out), .sel(comparator_28_eq));  // open: en
  Multiplexer #(.width(32)) multiplexer_55 (
    .in0(in29), .in1(wd_t), .out(multiplexer_55_out), .sel(comparator_29_eq));  // open: en
  Multiplexer #(.width(32)) multiplexer_56 (
    .in0(in30), .in1(wd_t), .out(multiplexer_56_out), .sel(comparator_30_eq));  // open: en
  Multiplexer #(.width(32)) multiplexer_57 (
    .in0(in31), .in1(wd_t), .out(multiplexer_57_out), .sel(comparator_31_eq));  // open: en
  Multiplexer #(.width(32)) multiplexer_58 (
    .in0(multiplexer_51_out), .in1({32{1'b0}}), .out(in25), .sel(re));  // open: en
  Multiplexer #(.width(32)) multiplexer_59 (
    .in0(multiplexer_52_out), .in1({32{1'b0}}), .out(in26), .sel(re));  // open: en
  Multiplexer #(.width(32)) multiplexer_60 (
    .in0(multiplexer_53_out), .in1({32{1'b0}}), .out(in27), .sel(re));  // open: en
  Multiplexer #(.width(32)) multiplexer_61 (
    .in0(multiplexer_54_out), .in1({32{1'b0}}), .out(in28), .sel(re));  // open: en
  Multiplexer #(.width(32)) multiplexer_62 (
    .in0(multiplexer_55_out), .in1({32{1'b0}}), .out(in29), .sel(re));  // open: en
  Multiplexer #(.width(32)) multiplexer_63 (
    .in0(multiplexer_56_out), .in1({32{1'b0}}), .out(in30), .sel(re));  // open: en
  Multiplexer #(.width(32)) multiplexer_64 (
    .in0(multiplexer_57_out), .in1({32{1'b0}}), .out(in31), .sel(re));  // open: en
endmodule

module qq (
  input  [31:0] WD
);

  wire and_1_out, comparator_1_eq, comparator_2_eq, comparator_2_lt, comparator_3_eq, comparator_4_eq,
       comparator_5_eq, comparator_6_eq, comparator_7_eq, comparator_8_eq, comparator_9_eq, comparator_10_eq,
       comparator_11_eq, comparator_12_eq, comparator_13_eq, comparator_14_eq, we;
  wire [4:0] a3;
  wire [31:0] demultiplexer_1_out0, in1, in2, in3, in4, in5, in6, in7, in8, in9, in10, in11, in12, in13,
       in14, in15, in16, in17, in18, in19, in20, in21, in22, in23, in24, in25, in26, in27, in28, in29, in30,
       in31, wd_t;

  // Probe on a3
  Demultiplexer #(.select(5), .width(32)) demultiplexer_1 (
    .out0(demultiplexer_1_out0), .out1(in1), .out2(in2), .out3(in3), .out4(in4), .out5(in5), .out6(in6),
    .out7(in7), .out8(in8), .out9(in9), .out10(in10), .out11(in11), .out12(in12), .out13(in13), .out14(in14),
    .out15(in15), .out16(in16), .out17(in17), .out18(in18), .out19(in19), .out20(in20), .out21(in21),
    .out22(in22), .out23(in23), .out24(in24), .out25(in25), .out26(in26), .out27(in27), .out28(in28),
    .out29(in29), .out30(in30), .out31(in31), .in(WD), .sel(a3), .en(1'b1));
  Comparator #(.width(5)) comparator_1 (.a(a3), .b(5'b00001), .eq(comparator_1_eq));  // open: gt, lt
  Comparator #(.width(5)) comparator_2 (.a(a3), .b(5'b00010), .eq(comparator_2_eq), .lt(comparator_2_lt));  // open: gt
  Comparator #(.width(5)) comparator_3 (.a(a3), .b(5'b00011), .eq(comparator_3_eq));  // open: gt, lt
  Comparator #(.width(5)) comparator_4 (.a(a3), .b(5'b00100), .eq(comparator_4_eq));  // open: gt, lt
  Comparator #(.width(5)) comparator_5 (.a(a3), .b(5'b00101), .eq(comparator_5_eq));  // open: gt, lt
  Comparator #(.width(5)) comparator_6 (.a(a3), .b(5'b00110), .eq(comparator_6_eq));  // open: gt, lt
  Comparator #(.width(5)) comparator_7 (.a(a3), .b(5'b00111), .eq(comparator_7_eq));  // open: gt, lt
  Comparator #(.width(5)) comparator_8 (.a(a3), .b(5'b01000), .eq(comparator_8_eq));  // open: gt, lt
  Comparator #(.width(5)) comparator_9 (.a(a3), .b(5'b01001), .eq(comparator_9_eq));  // open: gt, lt
  Comparator #(.width(5)) comparator_10 (.a(a3), .b(5'b01010), .eq(comparator_10_eq));  // open: gt, lt
  Comparator #(.width(5)) comparator_11 (.a(a3), .b(5'b01011), .eq(comparator_11_eq));  // open: gt, lt
  Comparator #(.width(5)) comparator_12 (.a(a3), .b(5'b01100), .eq(comparator_12_eq));  // open: gt, lt
  Comparator #(.width(5)) comparator_13 (.a(a3), .b(5'b01101), .eq(comparator_13_eq));  // open: gt, lt
  Comparator #(.width(5)) comparator_14 (.a(a3), .b(5'b01110), .eq(comparator_14_eq));  // open: gt, lt
  and and_1 (and_1_out, we, comparator_1_eq);
  Multiplexer #(.width(32)) multiplexer_1 (.in0(in1), .in1(wd_t), .out(in1), .sel(and_1_out));  // open: en
  Multiplexer #(.width(32)) multiplexer_2 (.in0(in2), .in1(wd_t), .out(in2), .sel(comparator_2_eq));  // open: en
  Multiplexer #(.width(32)) multiplexer_3 (.in0(in3), .in1(wd_t), .out(in3), .sel(comparator_3_eq));  // open: en
  Multiplexer #(.width(32)) multiplexer_4 (.in0(in4), .in1(wd_t), .out(in4), .sel(comparator_4_eq));  // open: en
  Multiplexer #(.width(32)) multiplexer_5 (.in0(in5), .in1(wd_t), .out(in5), .sel(comparator_5_eq));  // open: en
  Multiplexer #(.width(32)) multiplexer_6 (.in0(in6), .in1(wd_t), .out(in6), .sel(comparator_6_eq));  // open: en
  Multiplexer #(.width(32)) multiplexer_7 (.in0(in7), .in1(wd_t), .out(in7), .sel(comparator_7_eq));  // open: en
  Multiplexer #(.width(32)) multiplexer_8 (.in0(in8), .in1(wd_t), .out(in8), .sel(comparator_8_eq));  // open: en
  Multiplexer #(.width(32)) multiplexer_9 (.in0(in9), .in1(wd_t), .out(in9), .sel(comparator_9_eq));  // open: en
  Multiplexer #(.width(32)) multiplexer_10 (.in0(in10), .in1(wd_t), .out(in10), .sel(comparator_10_eq));  // open: en
  Multiplexer #(.width(32)) multiplexer_11 (.in0(in11), .in1(wd_t), .out(in11), .sel(comparator_11_eq));  // open: en
  Multiplexer #(.width(32)) multiplexer_12 (.in0(in12), .in1(wd_t), .out(in12), .sel(comparator_12_eq));  // open: en
  Multiplexer #(.width(32)) multiplexer_13 (.in0(in13), .in1(wd_t), .out(in13), .sel(comparator_13_eq));  // open: en
  Multiplexer #(.width(32)) multiplexer_14 (.in0(in14), .in1(wd_t), .out(in14), .sel(comparator_14_eq));  // open: en
endmodule

module qqq (
);

  wire comparator_1_eq, comparator_2_eq, comparator_3_eq, comparator_4_eq, comparator_5_eq, comparator_6_eq,
       comparator_7_eq, comparator_8_eq, comparator_9_eq, comparator_10_eq, comparator_11_eq,
       comparator_12_eq, comparator_13_eq, comparator_14_eq, comparator_15_eq, comparator_16_eq,
       comparator_17_eq;
  wire [4:0] a3;
  wire [31:0] in15, in16, in17, in18, in19, in20, in21, in22, in23, in24, in25, in26, in27, in28, in29, in30,
       in31, wd;

  Comparator #(.width(5)) comparator_1 (.a(a3), .b(5'b01111), .eq(comparator_1_eq));  // open: gt, lt
  Comparator #(.width(5)) comparator_2 (.a(a3), .b(5'b10000), .eq(comparator_2_eq));  // open: gt, lt
  Comparator #(.width(5)) comparator_3 (.a(a3), .b(5'b10001), .eq(comparator_3_eq));  // open: gt, lt
  Comparator #(.width(5)) comparator_4 (.a(a3), .b(5'b10010), .eq(comparator_4_eq));  // open: gt, lt
  Comparator #(.width(5)) comparator_5 (.a(a3), .b(5'b10011), .eq(comparator_5_eq));  // open: gt, lt
  Comparator #(.width(5)) comparator_6 (.a(a3), .b(5'b10100), .eq(comparator_6_eq));  // open: gt, lt
  Comparator #(.width(5)) comparator_7 (.a(a3), .b(5'b10101), .eq(comparator_7_eq));  // open: gt, lt
  Comparator #(.width(5)) comparator_8 (.a(a3), .b(5'b10110), .eq(comparator_8_eq));  // open: gt, lt
  Comparator #(.width(5)) comparator_9 (.a(a3), .b(5'b10111), .eq(comparator_9_eq));  // open: gt, lt
  Comparator #(.width(5)) comparator_10 (.a(a3), .b(5'b11000), .eq(comparator_10_eq));  // open: gt, lt
  Multiplexer #(.width(32)) multiplexer_1 (.in0(in15), .in1(wd), .out(in15), .sel(comparator_1_eq));  // open: en
  Multiplexer #(.width(32)) multiplexer_2 (.in0(in16), .in1(wd), .out(in16), .sel(comparator_2_eq));  // open: en
  Multiplexer #(.width(32)) multiplexer_3 (.in0(in17), .in1(wd), .out(in17), .sel(comparator_3_eq));  // open: en
  Multiplexer #(.width(32)) multiplexer_4 (.in0(in18), .in1(wd), .out(in18), .sel(comparator_4_eq));  // open: en
  Multiplexer #(.width(32)) multiplexer_5 (.in0(in19), .in1(wd), .out(in19), .sel(comparator_5_eq));  // open: en
  Multiplexer #(.width(32)) multiplexer_6 (.in0(in20), .in1(wd), .out(in20), .sel(comparator_6_eq));  // open: en
  Multiplexer #(.width(32)) multiplexer_7 (.in0(in21), .in1(wd), .out(in21), .sel(comparator_7_eq));  // open: en
  Multiplexer #(.width(32)) multiplexer_8 (.in0(in22), .in1(wd), .out(in22), .sel(comparator_8_eq));  // open: en
  Multiplexer #(.width(32)) multiplexer_9 (.in0(in23), .in1(wd), .out(in23), .sel(comparator_9_eq));  // open: en
  Multiplexer #(.width(32)) multiplexer_10 (.in0(in24), .in1(wd), .out(in24), .sel(comparator_10_eq));  // open: en
  Comparator #(.width(5)) comparator_11 (.a(a3), .b(5'b11001), .eq(comparator_11_eq));  // open: gt, lt
  Comparator #(.width(5)) comparator_12 (.a(a3), .b(5'b11010), .eq(comparator_12_eq));  // open: gt, lt
  Comparator #(.width(5)) comparator_13 (.a(a3), .b(5'b11011), .eq(comparator_13_eq));  // open: gt, lt
  Comparator #(.width(5)) comparator_14 (.a(a3), .b(5'b11100), .eq(comparator_14_eq));  // open: gt, lt
  Comparator #(.width(5)) comparator_15 (.a(a3), .b(5'b11101), .eq(comparator_15_eq));  // open: gt, lt
  Comparator #(.width(5)) comparator_16 (.a(a3), .b(5'b11110), .eq(comparator_16_eq));  // open: gt, lt
  Comparator #(.width(5)) comparator_17 (.a(a3), .b({5{1'b1}}), .eq(comparator_17_eq));  // open: gt, lt
  Multiplexer #(.width(32)) multiplexer_11 (.in0(in25), .in1(wd), .out(in25), .sel(comparator_11_eq));  // open: en
  Multiplexer #(.width(32)) multiplexer_12 (.in0(in26), .in1(wd), .out(in26), .sel(comparator_12_eq));  // open: en
  Multiplexer #(.width(32)) multiplexer_13 (.in0(in27), .in1(wd), .out(in27), .sel(comparator_13_eq));  // open: en
  Multiplexer #(.width(32)) multiplexer_14 (.in0(in28), .in1(wd), .out(in28), .sel(comparator_14_eq));  // open: en
  Multiplexer #(.width(32)) multiplexer_15 (.in0(in29), .in1(wd), .out(in29), .sel(comparator_15_eq));  // open: en
  Multiplexer #(.width(32)) multiplexer_16 (.in0(in30), .in1(wd), .out(in30), .sel(comparator_16_eq));  // open: en
  Multiplexer #(.width(32)) multiplexer_17 (.in0(in31), .in1(wd), .out(in31), .sel(comparator_17_eq));  // open: en
endmodule
