// Logisim project P0.L0.Q33.circ as structural Verilog
module grf (
  input  reset,
  input  [4:0] A1,
  input  in_3,
  input  WE,
  input  [4:0] A2,
  input  [4:0] A3,
  input  [31:0] WD,
  output [31:0] RD1,
  output [31:0] RD2
);

  wire [31:0] _0, _1, _2, _3, _4, _5, _6, _7, _8, _9, _10, _11, _12, _13, _14, _15, _16, _17, _18, _19, _20,
       _21, _22, _23, _24, _25, _26, _27, _28, _29, _30, _31, demultiplexer_1_out0, in1, in2, in3, in4, in5,
       in6, in7, in8, in9, in10, in11, in12, in13, in14, in15, in16, in17, in18, in19, in20, in21, in22,
       in23, in24, in25, in26, in27, in28, in29, in30, in31;

  // Probe on A3
  Demultiplexer #(.select(5), .width(32), .tristate("true")) demultiplexer_1 (
    .out0(demultiplexer_1_out0), .out1(in1), .out2(in2), .out3(in3), .out4(in4), .out5(in5), .out6(in6),
    .out7(in7), .out8(in8), .out9(in9), .out10(in10), .out11(in11), .out12(in12), .out13(in13), .out14(in14),
    .out15(in15), .out16(in16), .out17(in17), .out18(in18), .out19(in19), .out20(in20), .out21(in21),
    .out22(in22), .out23(in23), .out24(in24), .out25(in25), .out26(in26), .out27(in27), .out28(in28),
    .out29(in29), .out30(in30), .out31(in31), .in(WD), .sel(A3), .en(1'b1));
  Register #(.width(32)) register_1 (.D({32{1'b0}}), .en(WE), .Q(_0), .clk(in_3), .clr(reset));
  Register #(.width(32)) register_2 (.D(in4), .en(WE), .Q(_4), .clk(in_3), .clr(reset));
  Register #(.width(32)) register_3 (.D(in8), .en(WE), .Q(_8), .clk(in_3), .clr(reset));
  Register #(.width(32)) register_4 (.D(in12), .en(WE), .Q(_12), .clk(in_3), .clr(reset));
  Register #(.width(32)) register_5 (.D(in16), .en(WE), .Q(_16), .clk(in_3), .clr(reset));
  Register #(.width(32)) register_6 (.D(in20), .en(WE), .Q(_20), .clk(in_3), .clr(reset));
  Register #(.width(32)) register_7 (.D(in24), .en(WE), .Q(_24), .clk(in_3), .clr(reset));
  Register #(.width(32)) register_8 (.D(in28), .en(WE), .Q(_28), .clk(in_3), .clr(reset));
  Register #(.width(32)) register_9 (.D(in1), .en(WE), .Q(_1), .clk(in_3), .clr(reset));
  Register #(.width(32)) register_10 (.D(in5), .en(WE), .Q(_5), .clk(in_3), .clr(reset));
  Register #(.width(32)) register_11 (.D(in9), .en(WE), .Q(_9), .clk(in_3), .clr(reset));
  Register #(.width(32)) register_12 (.D(in13), .en(WE), .Q(_13), .clk(in_3), .clr(reset));
  Register #(.width(32)) register_13 (.D(in17), .en(WE), .Q(_17), .clk(in_3), .clr(reset));
  Register #(.width(32)) register_14 (.D(in21), .en(WE), .Q(_21), .clk(in_3), .clr(reset));
  Register #(.width(32)) register_15 (.D(in25), .en(WE), .Q(_25), .clk(in_3), .clr(reset));
  Register #(.width(32)) register_16 (.D(in29), .en(WE), .Q(_29), .clk(in_3), .clr(reset));
  Register #(.width(32)) register_17 (.D(in2), .en(WE), .Q(_2), .clk(in_3), .clr(reset));
  Register #(.width(32)) register_18 (.D(in6), .en(WE), .Q(_6), .clk(in_3), .clr(reset));
  Register #(.width(32)) register_19 (.D(in10), .en(WE), .Q(_10), .clk(in_3), .clr(reset));
  Register #(.width(32)) register_20 (.D(in14), .en(WE), .Q(_14), .clk(in_3), .clr(reset));
  Register #(.width(32)) register_21 (.D(in18), .en(WE), .Q(_18), .clk(in_3), .clr(reset));
  Register #(.width(32)) register_22 (.D(in22), .en(WE), .Q(_22), .clk(in_3), .clr(reset));
  Register #(.width(32)) register_23 (.D(in26), .en(WE), .Q(_26), .clk(in_3), .clr(reset));
  Register #(.width(32)) register_24 (.D(in30), .en(WE), .Q(_30), .clk(in_3), .clr(reset));
  Register #(.width(32)) register_25 (.D(in3), .en(WE), .Q(_3), .clk(in_3), .clr(reset));
  Register #(.width(32)) register_26 (.D(in7), .en(WE), .Q(_7), .clk(in_3), .clr(reset));
  Register #(.width(32)) register_27 (.D(in11), .en(WE), .Q(_11), .clk(in_3), .clr(reset));
  Register #(.width(32)) register_28 (.D(in15), .en(WE), .Q(_15), .clk(in_3), .clr(reset));
  Register #(.width(32)) register_29 (.D(in19), .en(WE), .Q(_19), .clk(in_3), .clr(reset));
  Register #(.width(32)) register_30 (.D(in23), .en(WE), .Q(_23), .clk(in_3), .clr(reset));
  Register #(.width(32)) register_31 (.D(in27), .en(WE), .Q(_27), .clk(in_3), .clr(reset));
  Register #(.width(32)) register_32 (.D(in31), .en(WE), .Q(_31), .clk(in_3), .clr(reset));
  Multiplexer #(.select(5), .width(32)) multiplexer_1 (
    .in0(_0), .in1(_1), .in2(_2), .in3(_3), .in4(_4), .in5(_5), .in6(_6), .in7(_7), .in8(_8), .in9(_9),
    .in10(_10), .in11(_11), .in12(_12), .in13(_13), .in14(_14), .in15(_15), .in16(_16), .in17(_17),
    .in18(_18), .in19(_19), .in20(_20), .in21(_21), .in22(_22), .in23(_23), .in24(_24), .in25(_25),
    .in26(_26), .in27(_27), .in28(_28), .in29(_29), .in30(_30), .in31(_31), .out(RD1), .sel(A1), .en(1'b1));
  Multiplexer #(.select(5), .width(32)) multiplexer_2 (
    .in0(_0), .in1(_1), .in2(_2), .in3(_3), .in4(_4), .in5(_5), .in6(_6), .in7(_7), .in8(_8), .in9(_9),
    .in10(_10), .in11(_11), .in12(_12), .in13(_13), .in14(_14), .in15(_15), .in16(_16), .in17(_17),
    .in18(_18), .in19(_19), .in20(_20), .in21(_21), .in22(_22), .in23(_23), .in24(_24), .in25(_25),
    .in26(_26), .in27(_27), .in28(_28), .in29(_29), .in30(_30), .in31(_31), .out(RD2), .sel(A2), .en(1'b1));

  // Other names for the same wires on the sheet: re = reset
endmodule
