// Logisim project P0.L0.Q44.circ as structural Verilog
module fsm (
  input  CLR,
  input  [1:0] In,
  output Z
);

  wire and_2_out, and_3_out, clock_1_out, not_1_out, not_2_out, not_3_out, not_4_out, not_5_out, register_1_q;
  wire [1:0] and_1_out, register_2_q;

  Clock clock_1 (.out(clock_1_out));
  not not_1 (not_1_out, register_2_q[0]);
  not not_2 (not_2_out, In[0]);
  not not_3 (not_3_out, In[1]);
  not not_4 (not_4_out, register_2_q[1]);
  Register #(.width(1)) register_1 (.D(CLR), .Q(register_1_q), .clk(clock_1_out), .clr(register_1_q));  // open: en
  and and_1 (and_1_out[0], not_1_out, register_2_q[1], not_2_out);
  and and_2 (and_2_out, not_3_out, In[0], not_1_out);
  and and_3 (and_3_out, not_4_out, register_2_q[0], not_3_out, In[0]);
  or or_1 (and_1_out[1], and_2_out, and_3_out);
  Register #(.width(2)) register_2 (
    .D(and_1_out), .Q(register_2_q), .clk(clock_1_out), .clr(register_1_q));  // open: en
  not not_5 (not_5_out, register_2_q[1]);
  and and_4 (Z, register_2_q[0], not_5_out, not_2_out);

  // Notes on the sheet:
  //   In0
  //   In1
  //   S1'
  //   S0'
  //   S1
  //   S0
endmodule
