// Logisim project P0.L0.Q444.circ as structural Verilog
module fsm (
  input  CLR,
  input  [1:0] In,
  output Z
);

  wire and_1_out, and_2_out, and_3_out, clock_1_out, not_1_out, not_2_out, not_3_out, not_4_out, not_5_out,
       or_1_out;
  wire [1:0] multiplexer_1_out, register_1_q;

  Clock clock_1 (.out(clock_1_out));
  not not_1 (not_1_out, register_1_q[0]);
  not not_2 (not_2_out, In[0]);
  not not_3 (not_3_out, In[1]);
  not not_4 (not_4_out, register_1_q[1]);
  and and_1 (and_1_out, not_1_out, register_1_q[1], not_2_out);
  and and_2 (and_2_out, not_3_out, In[0], not_1_out);
  and and_3 (and_3_out, not_4_out, register_1_q[0], not_3_out, In[0]);
  Multiplexer multiplexer_1 (.in0(and_1_out), .in1(1'b0), .out(multiplexer_1_out[0]), .sel(CLR));  // open: en
  or or_1 (or_1_out, and_2_out, and_3_out);
  Multiplexer multiplexer_2 (.in0(or_1_out), .in1(1'b0), .out(multiplexer_1_out[1]), .sel(CLR));  // open: en
  Register #(.width(2)) register_1 (.D(multiplexer_1_out), .Q(register_1_q), .clk(clock_1_out));  // open: en, clr
  not not_5 (not_5_out, register_1_q[1]);
  and and_4 (Z, register_1_q[0], not_5_out, not_2_out);

  // Notes on the sheet:
  //   In0
  //   In1
  //   S1'
  //   S0'
  //   S1
  //   S0
endmodule
