// Logisim project CPU.circ as structural Verilog: 13 circuits, main circuit main
module main (
  input  Reset,
  output [31:0] out_2,
  output out_3,
  output [4:0] out_4,
  output [31:0] out_5,
  output out_6,
  output [4:0] out_7,
  output [31:0] out_8
);

  wire alu_1_zero, ALUSrc, and_1_out, Branch, clk, EXTOp, MemRead, MemtoReg1, MemtoReg2, RegDst;
  wire [2:0] alucontrol_1_out_3, controller_1_aluop0;
  wire [4:0] PC_q_2;
  wire [31:0] adder_1_out, adder_2_out, alu_1_result, dm_1_rd, ext_1_out, grf_1_rd1, multiplexer_2_out,
       multiplexer_3_out, multiplexer_4_out, multiplexer_5_out, PC_q, shift_1_out_2, zero_ext_1_out;

  // Probe on PC_q_2
  IM im_1 (.A(PC_q_2), .RD(out_2));
  Controller controller_1 (
    .in_1(out_2[31:26]), .RegDst(RegDst), .ALUSrc(ALUSrc), .RegWrite(out_3), .MemRead(MemRead),
    .MemWrite(out_6), .MemtoReg1(MemtoReg1), .MemtoReg2(MemtoReg2), .EXTOp(EXTOp), .Branch(Branch),
    .ALUOp2(controller_1_aluop0[2]), .ALUOp1(controller_1_aluop0[1]), .ALUOp0(controller_1_aluop0[0]));
  Clock clock_1 (.out(clk));
  Register #(.width(32)) PC (
    .D(multiplexer_4_out), .Q({PC_q[31:7], PC_q_2, PC_q[1:0]}), .clk(clk), .clr(Reset));  // open: en
  Multiplexer #(.width(5)) multiplexer_1 (
    .in0(out_2[20:16]), .in1(out_2[15:11]), .out(out_4), .sel(RegDst));  // open: en
  ALUControl alucontrol_1 (.func(out_2[5:0]), .ALUop(controller_1_aluop0), .out_3(alucontrol_1_out_3));
  EXT ext_1 (.in(out_2[15:0]), .out(ext_1_out));
  Zero_EXT zero_ext_1 (.in(out_2[15:0]), .out(zero_ext_1_out));
  GRF grf_1 (
    .RA1(out_2[25:21]), .RA2(out_2[20:16]), .WA(out_4), .WD(out_5), .CLK(clk), .Reset(Reset),
    .RegWrite(out_3), .RD1(grf_1_rd1), .RD2(out_8));
  Multiplexer #(.width(32)) multiplexer_2 (
    .in0(ext_1_out), .in1(zero_ext_1_out), .out(multiplexer_2_out), .sel(EXTOp));  // open: en
  Adder #(.width(32)) adder_1 (.a(32'h4), .b({PC_q[31:7], PC_q_2, PC_q[1:0]}), .out(adder_1_out));  // open: cin, cout
  Shift shift_1 (.in_1(multiplexer_2_out), .out_2(shift_1_out_2));
  Multiplexer #(.width(32)) multiplexer_3 (
    .in0(out_8), .in1(multiplexer_2_out), .out(multiplexer_3_out), .sel(ALUSrc));  // open: en
  Adder #(.width(32)) adder_2 (.a(adder_1_out), .b(shift_1_out_2), .out(adder_2_out));  // open: cin, cout
  ALU alu_1 (
    .A(grf_1_rd1), .B(multiplexer_3_out), .ALUCtrl(alucontrol_1_out_3),
    .Result({alu_1_result[31:7], out_7, alu_1_result[1:0]}), .Zero(alu_1_zero));
  Multiplexer #(.width(32)) multiplexer_4 (
    .in0(adder_1_out), .in1(adder_2_out), .out(multiplexer_4_out), .sel(and_1_out));  // open: en
  and and_1 (and_1_out, alu_1_zero, Branch);
  DM dm_1 (.A(out_7), .WD(out_8), .CLK(clk), .MemRead(MemRead), .MemWrite(out_6), .RD(dm_1_rd), .clr(Reset));
  Multiplexer #(.width(32)) multiplexer_5 (
    .in0({alu_1_result[31:7], out_7, alu_1_result[1:0]}), .in1(dm_1_rd), .out(multiplexer_5_out),
    .sel(MemtoReg1));  // open: en
  Multiplexer #(.width(32)) multiplexer_6 (
    .in0(multiplexer_5_out), .in1({out_2[15:0], {16{1'b0}}}), .out(out_5), .sel(MemtoReg2));  // open: en

  // Other names for the same wires on the sheet: Instr[31:0] = out_2; MemAddr[4:0] = out_7; MemData[31:0] = out_8;
  //   MemWrite = out_6; RegAddr[4:0] = out_4; RegData[31:0] = out_5; RegWrite = out_3

  // Notes on the sheet:
  //   OP
  //   func
  //   Rt
  //   Rd
  //   Rs
  //   RegDst
  //   imm16
  //   RD1
  //     RD2
  //   WD
  //   RegWrite
  //   EXTOp
  //   Adder
  //    ALUSrc
  //   Nadd
  //   ALUStr
  //   Zero
  //        PCSrc
  //   Branch
  //   MemRead
  //   MemWrite
  //   A
  //   RD
  //   WD
  //   MemtoReg1
  //   MemtoReg2
endmodule

module ALU (
  input  [31:0] A,
  input  [31:0] B,
  input  [2:0] ALUCtrl,
  output [31:0] Result,
  output Zero
);

  wire or_1_out;
  wire [0:0] comparator_1_gt;
  wire [3:0] n4bitalu_1_out_3, n4bitalu_1_out_4, n4bitalu_2_out_3, n4bitalu_2_out_4, n4bitalu_3_out_3,
       n4bitalu_3_out_4, n4bitalu_4_out_3, n4bitalu_4_out_4, n4bitalu_5_out_3, n4bitalu_5_out_4,
       n4bitalu_6_out_3, n4bitalu_6_out_4, n4bitalu_7_out_3, n4bitalu_7_out_4, n4bitalu_8_out_3,
       n4bitalu_8_out_4;
  wire [31:0] adder_1_out, subtractor_1_out;

  Adder #(.width(32)) adder_1 (.a(A), .b(B), .out(adder_1_out));  // open: cin, cout
  Subtractor #(.width(32)) subtractor_1 (.a(A), .b(B), .out(subtractor_1_out));  // open: bin, bout
  Comparator #(.width(32), .mode("unsigned")) comparator_1 (.a(A), .b(B), .gt(comparator_1_gt[0]));  // open: eq, lt
  _4bitalu u_4bitalu_1 (.in_1(A[3:0]), .in_2(B[3:0]), .out_3(n4bitalu_1_out_3), .out_4(n4bitalu_1_out_4));
  _4bitalu u_4bitalu_2 (.in_1(A[7:4]), .in_2(B[7:4]), .out_3(n4bitalu_2_out_3), .out_4(n4bitalu_2_out_4));
  _4bitalu u_4bitalu_3 (.in_1(A[11:8]), .in_2(B[11:8]), .out_3(n4bitalu_3_out_3), .out_4(n4bitalu_3_out_4));
  _4bitalu u_4bitalu_4 (.in_1(A[15:12]), .in_2(B[15:12]), .out_3(n4bitalu_4_out_3), .out_4(n4bitalu_4_out_4));
  _4bitalu u_4bitalu_5 (.in_1(A[19:16]), .in_2(B[19:16]), .out_3(n4bitalu_5_out_3), .out_4(n4bitalu_5_out_4));
  _4bitalu u_4bitalu_6 (.in_1(A[23:20]), .in_2(B[23:20]), .out_3(n4bitalu_6_out_3), .out_4(n4bitalu_6_out_4));
  _4bitalu u_4bitalu_7 (.in_1(A[27:24]), .in_2(B[27:24]), .out_3(n4bitalu_7_out_3), .out_4(n4bitalu_7_out_4));
  _4bitalu u_4bitalu_8 (.in_1(A[31:28]), .in_2(B[31:28]), .out_3(n4bitalu_8_out_3), .out_4(n4bitalu_8_out_4));
  Multiplexer #(.select(3), .width(32)) multiplexer_1 (
    .in0({n4bitalu_8_out_3, n4bitalu_7_out_3, n4bitalu_6_out_3, n4bitalu_5_out_3, n4bitalu_4_out_3, n4bitalu_3_out_3, n4bitalu_2_out_3, n4bitalu_1_out_3}),
    .in1({n4bitalu_8_out_4, n4bitalu_7_out_4, n4bitalu_6_out_4, n4bitalu_5_out_4, n4bitalu_4_out_4, n4bitalu_3_out_4, n4bitalu_2_out_4, n4bitalu_1_out_4}),
    .in2(adder_1_out), .in5({{31{1'b0}}, comparator_1_gt[0]}), .in6(subtractor_1_out), .out(Result),
    .sel(ALUCtrl));  // open: in3, in4, in7, en
  or or_1 (or_1_out, subtractor_1_out[0], subtractor_1_out[1], subtractor_1_out[2], subtractor_1_out[3], subtractor_1_out[4], subtractor_1_out[5], subtractor_1_out[6], subtractor_1_out[7], subtractor_1_out[8], subtractor_1_out[9], subtractor_1_out[10], subtractor_1_out[11], subtractor_1_out[12], subtractor_1_out[13], subtractor_1_out[14], subtractor_1_out[15], subtractor_1_out[17], subtractor_1_out[18], subtractor_1_out[19], subtractor_1_out[20], subtractor_1_out[21], subtractor_1_out[22], subtractor_1_out[23], subtractor_1_out[24], subtractor_1_out[25], subtractor_1_out[26], subtractor_1_out[27], subtractor_1_out[28], subtractor_1_out[29], subtractor_1_out[30], subtractor_1_out[31], subtractor_1_out[16]);
  not not_1 (Zero, or_1_out);
endmodule

module _4bitalu (
  input  [3:0] in_1,
  input  [3:0] in_2,
  output [3:0] out_3,
  output [3:0] out_4
);

  and and_1 (out_3[0], in_1[0], in_2[0]);
  and and_2 (out_3[1], in_1[1], in_2[1]);
  and and_3 (out_3[2], in_1[2], in_2[2]);
  and and_4 (out_3[3], in_1[3], in_2[3]);
  or or_1 (out_4[0], in_1[0], in_2[0]);
  or or_2 (out_4[1], in_1[1], in_2[1]);
  or or_3 (out_4[2], in_1[2], in_2[2]);
  or or_4 (out_4[3], in_1[3], in_2[3]);
endmodule

module GRF (
  input  [4:0] RA1,
  input  CLK,
  input  Reset,
  input  RegWrite,
  input  [4:0] RA2,
  input  [4:0] WA,
  input  [31:0] WD,
  output [31:0] RD1,
  output [31:0] RD2
);

  wire [31:0] _0, _1, _2, _3, _4, _5, _6, _7, _8, _9, _10, _11, _12, _13, _14, _15, _16, _17, _18, _19, _20,
       _21, _22, _23, _24, _25, _26, _27, _28, _29, _30, _31, demultiplexer_1_out0, in1, in2, in3, in4, in5,
       in6, in7, in8, in9, in10, in11, in12, in13, in14, in15, in16, in17, in18, in19, in20, in21, in22,
       in23, in24, in25, in26, in27, in28, in29, in30, in31;

  Demultiplexer #(.select(5), .width(32), .tristate("true")) demultiplexer_1 (
    .out0(demultiplexer_1_out0), .out1(in1), .out2(in2), .out3(in3), .out4(in4), .out5(in5), .out6(in6),
    .out7(in7), .out8(in8), .out9(in9), .out10(in10), .out11(in11), .out12(in12), .out13(in13), .out14(in14),
    .out15(in15), .out16(in16), .out17(in17), .out18(in18), .out19(in19), .out20(in20), .out21(in21),
    .out22(in22), .out23(in23), .out24(in24), .out25(in25), .out26(in26), .out27(in27), .out28(in28),
    .out29(in29), .out30(in30), .out31(in31), .in(WD), .sel(WA));  // open: en
  Register #(.width(32)) register_1 (.D({32{1'b0}}), .en(RegWrite), .Q(_0), .clk(CLK), .clr(Reset));
  Register #(.width(32)) register_2 (.D(in4), .en(RegWrite), .Q(_4), .clk(CLK), .clr(Reset));
  Register #(.width(32)) register_3 (.D(in8), .en(RegWrite), .Q(_8), .clk(CLK), .clr(Reset));
  Register #(.width(32)) register_4 (.D(in12), .en(RegWrite), .Q(_12), .clk(CLK), .clr(Reset));
  Register #(.width(32)) register_5 (.D(in16), .en(RegWrite), .Q(_16), .clk(CLK), .clr(Reset));
  Register #(.width(32)) register_6 (.D(in20), .en(RegWrite), .Q(_20), .clk(CLK), .clr(Reset));
  Register #(.width(32)) register_7 (.D(in24), .en(RegWrite), .Q(_24), .clk(CLK), .clr(Reset));
  Register #(.width(32)) register_8 (.D(in28), .en(RegWrite), .Q(_28), .clk(CLK), .clr(Reset));
  Register #(.width(32)) register_9 (.D(in1), .en(RegWrite), .Q(_1), .clk(CLK), .clr(Reset));
  Register #(.width(32)) register_10 (.D(in5), .en(RegWrite), .Q(_5), .clk(CLK), .clr(Reset));
  Register #(.width(32)) register_11 (.D(in9), .en(RegWrite), .Q(_9), .clk(CLK), .clr(Reset));
  Register #(.width(32)) register_12 (.D(in13), .en(RegWrite), .Q(_13), .clk(CLK), .clr(Reset));
  Register #(.width(32)) register_13 (.D(in17), .en(RegWrite), .Q(_17), .clk(CLK), .clr(Reset));
  Register #(.width(32)) register_14 (.D(in21), .en(RegWrite), .Q(_21), .clk(CLK), .clr(Reset));
  Register #(.width(32)) register_15 (.D(in25), .en(RegWrite), .Q(_25), .clk(CLK), .clr(Reset));
  Register #(.width(32)) register_16 (.D(in29), .en(RegWrite), .Q(_29), .clk(CLK), .clr(Reset));
  Register #(.width(32)) register_17 (.D(in2), .en(RegWrite), .Q(_2), .clk(CLK), .clr(Reset));
  Register #(.width(32)) register_18 (.D(in6), .en(RegWrite), .Q(_6), .clk(CLK), .clr(Reset));
  Register #(.width(32)) register_19 (.D(in10), .en(RegWrite), .Q(_10), .clk(CLK), .clr(Reset));
  Register #(.width(32)) register_20 (.D(in14), .en(RegWrite), .Q(_14), .clk(CLK), .clr(Reset));
  Register #(.width(32)) register_21 (.D(in18), .en(RegWrite), .Q(_18), .clk(CLK), .clr(Reset));
  Register #(.width(32)) register_22 (.D(in22), .en(RegWrite), .Q(_22), .clk(CLK), .clr(Reset));
  Register #(.width(32)) register_23 (.D(in26), .en(RegWrite), .Q(_26), .clk(CLK), .clr(Reset));
  Register #(.width(32)) register_24 (.D(in30), .en(RegWrite), .Q(_30), .clk(CLK), .clr(Reset));
  Register #(.width(32)) register_25 (.D(in3), .en(RegWrite), .Q(_3), .clk(CLK), .clr(Reset));
  Register #(.width(32)) register_26 (.D(in7), .en(RegWrite), .Q(_7), .clk(CLK), .clr(Reset));
  Register #(.width(32)) register_27 (.D(in11), .en(RegWrite), .Q(_11), .clk(CLK), .clr(Reset));
  Register #(.width(32)) register_28 (.D(in15), .en(RegWrite), .Q(_15), .clk(CLK), .clr(Reset));
  Register #(.width(32)) register_29 (.D(in19), .en(RegWrite), .Q(_19), .clk(CLK), .clr(Reset));
  Register #(.width(32)) register_30 (.D(in23), .en(RegWrite), .Q(_23), .clk(CLK), .clr(Reset));
  Register #(.width(32)) register_31 (.D(in27), .en(RegWrite), .Q(_27), .clk(CLK), .clr(Reset));
  Register #(.width(32)) register_32 (.D(in31), .en(RegWrite), .Q(_31), .clk(CLK), .clr(Reset));
  Multiplexer #(.select(5), .width(32)) multiplexer_1 (
    .in0(_0), .in1(_1), .in2(_2), .in3(_3), .in4(_4), .in5(_5), .in6(_6), .in7(_7), .in8(_8), .in9(_9),
    .in10(_10), .in11(_11), .in12(_12), .in13(_13), .in14(_14), .in15(_15), .in16(_16), .in17(_17),
    .in18(_18), .in19(_19), .in20(_20), .in21(_21), .in22(_22), .in23(_23), .in24(_24), .in25(_25),
    .in26(_26), .in27(_27), .in28(_28), .in29(_29), .in30(_30), .in31(_31), .out(RD1), .sel(RA1));  // open: en
  Multiplexer #(.select(5), .width(32)) multiplexer_2 (
    .in0(_0), .in1(_1), .in2(_2), .in3(_3), .in4(_4), .in5(_5), .in6(_6), .in7(_7), .in8(_8), .in9(_9),
    .in10(_10), .in11(_11), .in12(_12), .in13(_13), .in14(_14), .in15(_15), .in16(_16), .in17(_17),
    .in18(_18), .in19(_19), .in20(_20), .in21(_21), .in22(_22), .in23(_23), .in24(_24), .in25(_25),
    .in26(_26), .in27(_27), .in28(_28), .in29(_29), .in30(_30), .in31(_31), .out(RD2), .sel(RA2));  // open: en

  // Other names for the same wires on the sheet: a1[4:0] = RA1; a2[4:0] = RA2; a3[4:0] = WA
endmodule

module DM (
  input  [4:0] A,
  input  [31:0] WD,
  input  CLK,
  input  clr,
  input  MemWrite,
  input  MemRead,
  output [31:0] RD
);

  RAM #(.addrWidth(5), .dataWidth(32), .bus("separate")) ram_1 (
    .addr(A), .din(WD), .data(RD), .str(MemWrite), .clk(CLK), .ld(MemRead), .clr(clr));  // open: sel
endmodule

module IM (
  input  [4:0] A,
  output [31:0] RD
);

  ROM #(.addrWidth(5), .dataWidth(32)) rom_1 (.addr(A), .data(RD));  // open: sel

  // Notes on the sheet:
  //   contents of rom_1 (hex, n*v repeats v):
  //   3408006f 34090001 1094021 350a000c 12a4021 340b03e8 34e7ffff 3c050064 34050457 0 16a5821 14a5021
  //   114b0009 ad490000 8d4f0000 8d570000 1e57823 4821 ad2f0004 8d300004 1405821 116afff4 1495021
endmodule

module GRF2 (
  input  [4:0] RA1,
  input  [4:0] RA2,
  input  [4:0] WA,
  input  reset,
  input  WE,
  input  [31:0] WD,
  input  RegWrite,
  output [31:0] RD1,
  output [31:0] RD2
);

  wire clock_1_out;
  wire [31:0] _0, _1, _2, _3, _4, _5, _6, _7, _8, _9, _10, _11, _12, _13, _14, _15, _16, _17, _18, _19, _20,
       _21, _22, _23, _24, _25, _26, _27, _28, _29, _30, _31, in1, in2, in3, in4, in5, in6, in7, in8, in9,
       in10, in11, in12, in13, in14, in15, in16, in17, in18, in19, in20, in21, in22, in23, in24, in25, in26,
       in27, in28, in29, in30, in31;

  Decoder #(.select(5)) decoder_1 (.sel(WA));  // open: out0, out1, out2, out3, out4, out5, out6, out7, out8, out9, out10, out11, out12, out13, out14, out15, out16, out17, out18, out19, out20, out21, out22, out23, out24, out25, out26, out27, out28, out29, out30, out31, en
  Clock clock_1 (.out(clock_1_out));
  Register #(.width(32)) register_1 (.D({32{1'b0}}), .en(WE), .Q(_0), .clk(clock_1_out), .clr(reset));
  Register #(.width(32)) register_2 (.D(in4), .en(WE), .Q(_4), .clk(clock_1_out), .clr(reset));
  Register #(.width(32)) register_3 (.D(in8), .en(WE), .Q(_8), .clk(clock_1_out), .clr(reset));
  Register #(.width(32)) register_4 (.D(in12), .en(WE), .Q(_12), .clk(clock_1_out), .clr(reset));
  Register #(.width(32)) register_5 (.D(in16), .en(WE), .Q(_16), .clk(clock_1_out), .clr(reset));
  Register #(.width(32)) register_6 (.D(in20), .en(WE), .Q(_20), .clk(clock_1_out), .clr(reset));
  Register #(.width(32)) register_7 (.D(in24), .en(WE), .Q(_24), .clk(clock_1_out), .clr(reset));
  Register #(.width(32)) register_8 (.D(in28), .en(WE), .Q(_28), .clk(clock_1_out), .clr(reset));
  Register #(.width(32)) register_9 (.D(in1), .en(WE), .Q(_1), .clk(clock_1_out), .clr(reset));
  Register #(.width(32)) register_10 (.D(in5), .en(WE), .Q(_5), .clk(clock_1_out), .clr(reset));
  Register #(.width(32)) register_11 (.D(in9), .en(WE), .Q(_9), .clk(clock_1_out), .clr(reset));
  Register #(.width(32)) register_12 (.D(in13), .en(WE), .Q(_13), .clk(clock_1_out), .clr(reset));
  Register #(.width(32)) register_13 (.D(in17), .en(WE), .Q(_17), .clk(clock_1_out), .clr(reset));
  Register #(.width(32)) register_14 (.D(in21), .en(WE), .Q(_21), .clk(clock_1_out), .clr(reset));
  Register #(.width(32)) register_15 (.D(in25), .en(WE), .Q(_25), .clk(clock_1_out), .clr(reset));
  Register #(.width(32)) register_16 (.D(in29), .en(WE), .Q(_29), .clk(clock_1_out), .clr(reset));
  Register #(.width(32)) register_17 (.D(in2), .en(WE), .Q(_2), .clk(clock_1_out), .clr(reset));
  Register #(.width(32)) register_18 (.D(in6), .en(WE), .Q(_6), .clk(clock_1_out), .clr(reset));
  Register #(.width(32)) register_19 (.D(in10), .en(WE), .Q(_10), .clk(clock_1_out), .clr(reset));
  Register #(.width(32)) register_20 (.D(in14), .en(WE), .Q(_14), .clk(clock_1_out), .clr(reset));
  Register #(.width(32)) register_21 (.D(in18), .en(WE), .Q(_18), .clk(clock_1_out), .clr(reset));
  Register #(.width(32)) register_22 (.D(in22), .en(WE), .Q(_22), .clk(clock_1_out), .clr(reset));
  Register #(.width(32)) register_23 (.D(in26), .en(WE), .Q(_26), .clk(clock_1_out), .clr(reset));
  Register #(.width(32)) register_24 (.D(in30), .en(WE), .Q(_30), .clk(clock_1_out), .clr(reset));
  Register #(.width(32)) register_25 (.D(in3), .en(WE), .Q(_3), .clk(clock_1_out), .clr(reset));
  Register #(.width(32)) register_26 (.D(in7), .en(WE), .Q(_7), .clk(clock_1_out), .clr(reset));
  Register #(.width(32)) register_27 (.D(in11), .en(WE), .Q(_11), .clk(clock_1_out), .clr(reset));
  Register #(.width(32)) register_28 (.D(in15), .en(WE), .Q(_15), .clk(clock_1_out), .clr(reset));
  Register #(.width(32)) register_29 (.D(in19), .en(WE), .Q(_19), .clk(clock_1_out), .clr(reset));
  Register #(.width(32)) register_30 (.D(in23), .en(WE), .Q(_23), .clk(clock_1_out), .clr(reset));
  Register #(.width(32)) register_31 (.D(in27), .en(WE), .Q(_27), .clk(clock_1_out), .clr(reset));
  Register #(.width(32)) register_32 (.D(in31), .en(WE), .Q(_31), .clk(clock_1_out), .clr(reset));
  Multiplexer #(.select(5), .width(32)) multiplexer_1 (
    .in0(_0), .in1(_1), .in2(_2), .in3(_3), .in4(_4), .in5(_5), .in6(_6), .in7(_7), .in8(_8), .in9(_9),
    .in10(_10), .in11(_11), .in12(_12), .in13(_13), .in14(_14), .in15(_15), .in16(_16), .in17(_17),
    .in18(_18), .in19(_19), .in20(_20), .in21(_21), .in22(_22), .in23(_23), .in24(_24), .in25(_25),
    .in26(_26), .in27(_27), .in28(_28), .in29(_29), .in30(_30), .in31(_31), .out(RD1), .sel(RA1));  // open: en
  Multiplexer #(.select(5), .width(32)) multiplexer_2 (
    .in0(_0), .in1(_1), .in2(_2), .in3(_3), .in4(_4), .in5(_5), .in6(_6), .in7(_7), .in8(_8), .in9(_9),
    .in10(_10), .in11(_11), .in12(_12), .in13(_13), .in14(_14), .in15(_15), .in16(_16), .in17(_17),
    .in18(_18), .in19(_19), .in20(_20), .in21(_21), .in22(_22), .in23(_23), .in24(_24), .in25(_25),
    .in26(_26), .in27(_27), .in28(_28), .in29(_29), .in30(_30), .in31(_31), .out(RD2), .sel(RA2));  // open: en

  // Other names for the same wires on the sheet: a1[4:0] = RA1; a2[4:0] = RA2; a3[4:0] = WA
endmodule

// Sign
module EXT (
  input  [15:0] in,
  output [31:0] out
);

  assign out = {{16{in[15]}}, in};  // Bit_Extender bit_extender_1
endmodule

module IFU (
);

  wire clock_1_out;
  wire [31:0] adder_1_out, PC_q;

  Register #(.width(32)) PC (.D(adder_1_out), .Q(PC_q), .clk(clock_1_out));  // open: en, clr
  Clock clock_1 (.out(clock_1_out));
  Adder #(.width(32)) adder_1 (.a(32'h4), .b(PC_q), .out(adder_1_out));  // open: cin, cout
  IM im_1 ();  // open: A, RD
endmodule

module Shift (
  input  [31:0] in_1,
  output [31:0] out_2
);


  assign out_2 = {in_1[29:0], 2'b00};
endmodule

module Controller (
  input  [5:0] in_1,
  output RegDst,
  output ALUSrc,
  output RegWrite,
  output MemRead,
  output MemWrite,
  output MemtoReg1,
  output MemtoReg2,
  output EXTOp,
  output Branch,
  output ALUOp2,
  output ALUOp1,
  output ALUOp0
);

  wire not_1_out, not_2_out, not_3_out, not_4_out, not_5_out, not_6_out;

  not not_1 (not_1_out, in_1[5]);
  not not_2 (not_2_out, in_1[4]);
  not not_3 (not_3_out, in_1[3]);
  not not_4 (not_4_out, in_1[2]);
  not not_5 (not_5_out, in_1[1]);
  not not_6 (not_6_out, in_1[0]);
  and R (RegDst, not_1_out, not_2_out, not_3_out, not_4_out, not_5_out, not_6_out);
  and lw (MemRead, in_1[5], not_2_out, not_3_out, not_4_out, in_1[1], in_1[0]);
  and sw (MemWrite, in_1[5], not_2_out, in_1[3], not_4_out, in_1[1], in_1[0]);
  and beq (Branch, not_1_out, not_2_out, not_3_out, in_1[2], not_5_out, not_6_out);
  and lui (MemtoReg2, not_1_out, not_2_out, in_1[3], in_1[2], in_1[1], in_1[0]);
  and ori (ALUOp2, not_1_out, not_2_out, in_1[3], in_1[2], not_5_out, in_1[0]);
  // AND_Gate nop is placed but not wired
  or or_1 (ALUSrc, MemRead, MemWrite, ALUOp2);
  or or_2 (RegWrite, RegDst, MemRead, MemtoReg2, ALUOp2);
  or or_3 (ALUOp1, Branch, MemtoReg2, ALUOp2);
  or or_4 (ALUOp0, MemRead, MemWrite, MemtoReg2, ALUOp2);

  assign EXTOp = ALUOp2;
  assign MemtoReg1 = MemRead;
endmodule

// Zero
module Zero_EXT (
  input  [15:0] in,
  output [31:0] out
);

  assign out = {{16{1'b0}}, in};  // Bit_Extender bit_extender_1
endmodule

module ALUControl (
  input  [5:0] func,
  input  [2:0] ALUop,
  output [2:0] out_3
);

  wire addu_out, beq_out, lui_out, lw_out, not_1_out, not_2_out, not_3_out, not_4_out, not_5_out, not_6_out,
       not_7_out, not_8_out, not_9_out, ori_out, subu_out, sw_out;

  not not_1 (not_1_out, ALUop[2]);
  not not_2 (not_2_out, ALUop[0]);
  not not_3 (not_3_out, ALUop[1]);
  not not_4 (not_4_out, func[5]);
  not not_5 (not_5_out, func[4]);
  not not_6 (not_6_out, func[3]);
  not not_7 (not_7_out, func[2]);
  not not_8 (not_8_out, func[0]);
  not not_9 (not_9_out, func[1]);
  and lw (lw_out, not_1_out, not_3_out, ALUop[0]);
  and sw (sw_out, not_1_out, not_3_out, ALUop[0]);
  and beq (beq_out, not_1_out, ALUop[1], not_2_out);
  and lui (lui_out, not_1_out, ALUop[1], ALUop[0]);
  and ori (ori_out, ALUop[2], ALUop[1], ALUop[0]);
  and addu (addu_out, not_1_out, not_3_out, not_2_out, func[5], not_5_out, not_6_out, not_7_out, not_9_out, func[0]);
  and subu (subu_out, not_1_out, not_3_out, not_2_out, func[5], not_5_out, not_6_out, not_7_out, func[1], func[0]);
  or or_1 (out_3[2], beq_out, lui_out, subu_out);
  or or_2 (out_3[0], lui_out, ori_out);
  or or_3 (out_3[1], beq_out, lw_out, sw_out, addu_out, subu_out, lui_out);
endmodule
